// Logisim project ALL.circ as structural Verilog: 16 circuits, main circuit main
module main (
  input  in_1,
  output out_2
);

  nand nand_1 (out_2, in_1, in_1);
endmodule

module My_AND (
  input  in_1,
  input  in_2,
  output out_3
);

  wire nand_1_out;

  nand nand_1 (nand_1_out, in_1, in_2);
  nand nand_2 (out_3, nand_1_out, nand_1_out);
endmodule

module My_NOT (
  input  in_1,
  output out_2
);

  nand nand_1 (out_2, in_1, in_1);
endmodule

module My_Mux (
  input  a,
  input  b,
  input  sel,
  output out_4
);

  wire my_and_1_out_3, my_and_2_out_3, my_not_1_out_2;

  My_NOT my_not_1 (.in_1(sel), .out_2(my_not_1_out_2));
  My_AND my_and_1 (.in_1(a), .in_2(my_not_1_out_2), .out_3(my_and_1_out_3));
  My_AND my_and_2 (.in_1(b), .in_2(sel), .out_3(my_and_2_out_3));
  My_OR my_or_1 (.in_1(my_and_1_out_3), .in_2(my_and_2_out_3), .out_3(out_4));
endmodule

module My_OR (
  input  in_1,
  input  in_2,
  output out_3
);

  wire my_and_1_out_3, my_not_1_out_2, my_not_2_out_2;

  My_NOT my_not_1 (.in_1(in_1), .out_2(my_not_1_out_2));
  My_NOT my_not_2 (.in_1(in_2), .out_2(my_not_2_out_2));
  My_AND my_and_1 (.in_1(my_not_1_out_2), .in_2(my_not_2_out_2), .out_3(my_and_1_out_3));
  My_NOT my_not_3 (.in_1(my_and_1_out_3), .out_2(out_3));
endmodule

module My_XOR (
  input  in_1,
  input  in_2,
  output out_3
);

  wire my_and_1_out_3, my_and_2_out_3, my_not_1_out_2, my_not_2_out_2;

  My_NOT my_not_1 (.in_1(in_2), .out_2(my_not_1_out_2));
  My_NOT my_not_2 (.in_1(in_1), .out_2(my_not_2_out_2));
  My_AND my_and_1 (.in_1(in_1), .in_2(my_not_1_out_2), .out_3(my_and_1_out_3));
  My_AND my_and_2 (.in_1(my_not_2_out_2), .in_2(in_2), .out_3(my_and_2_out_3));
  My_OR my_or_1 (.in_1(my_and_1_out_3), .in_2(my_and_2_out_3), .out_3(out_3));
endmodule

module My_DMux (
  input  in,
  input  sel,
  output a,
  output b
);

  wire my_not_1_out_2;

  My_NOT my_not_1 (.in_1(sel), .out_2(my_not_1_out_2));
  My_AND my_and_1 (.in_1(in), .in_2(my_not_1_out_2), .out_3(a));
  My_AND my_and_2 (.in_1(in), .in_2(sel), .out_3(b));
endmodule

module My_Not4 (
  input  [3:0] a,
  output [3:0] out_2
);

  My_NOT my_not_1 (.in_1(a[0]), .out_2(out_2[0]));
  My_NOT my_not_2 (.in_1(a[1]), .out_2(out_2[1]));
  My_NOT my_not_3 (.in_1(a[2]), .out_2(out_2[2]));
  My_NOT my_not_4 (.in_1(a[3]), .out_2(out_2[3]));
endmodule

module My_AND4 (
  input  [3:0] in_1,
  input  [3:0] in_2,
  output [3:0] out_3
);

  My_AND my_and_1 (.in_1(in_1[0]), .in_2(in_2[0]), .out_3(out_3[0]));
  My_AND my_and_2 (.in_1(in_1[1]), .in_2(in_2[1]), .out_3(out_3[1]));
  My_AND my_and_3 (.in_1(in_1[2]), .in_2(in_2[2]), .out_3(out_3[2]));
  My_AND my_and_4 (.in_1(in_1[3]), .in_2(in_2[3]), .out_3(out_3[3]));
endmodule

module My_OR4 (
  input  [3:0] in_1,
  input  [3:0] in_2,
  output [3:0] out_3
);

  My_OR my_or_1 (.in_1(in_1[0]), .in_2(in_2[0]), .out_3(out_3[0]));
  My_OR my_or_2 (.in_1(in_1[1]), .in_2(in_2[1]), .out_3(out_3[1]));
  My_OR my_or_3 (.in_1(in_1[2]), .in_2(in_2[2]), .out_3(out_3[2]));
  My_OR my_or_4 (.in_1(in_1[3]), .in_2(in_2[3]), .out_3(out_3[3]));
endmodule

module My_Mux4 (
  input  [3:0] in_1,
  input  [3:0] in_2,
  input  in_3,
  output [3:0] out_4
);

  // My_Mux my_mux_1: pin names not known; wires that end beside it: in_1[0], in_2[0], in_3, out_4[0], out_4[1]
  // My_Mux my_mux_2: pin names not known; wires that end beside it: in_1[1], in_2[1], in_3, out_4[0], out_4[1], out_4[2]
  // My_Mux my_mux_3: pin names not known; wires that end beside it: in_1[2], in_2[2], in_3, out_4[1], out_4[2], out_4[3]
  // My_Mux my_mux_4: pin names not known; wires that end beside it: in_1[3], in_2[3], in_3, out_4[2], out_4[3]
endmodule

module My_Or8Way (
  input  [7:0] in_1,
  output out_2
);

  wire my_or_1_out_3, my_or_2_out_3, my_or_3_out_3, my_or_4_out_3, my_or_5_out_3, my_or_6_out_3;

  My_OR my_or_1 (.in_1(in_1[0]), .in_2(in_1[1]), .out_3(my_or_1_out_3));
  My_OR my_or_2 (.in_1(in_1[2]), .in_2(in_1[3]), .out_3(my_or_2_out_3));
  My_OR my_or_3 (.in_1(in_1[4]), .in_2(in_1[5]), .out_3(my_or_3_out_3));
  My_OR my_or_4 (.in_1(in_1[6]), .in_2(in_1[7]), .out_3(my_or_4_out_3));
  My_OR my_or_5 (.in_1(my_or_1_out_3), .in_2(my_or_2_out_3), .out_3(my_or_5_out_3));
  My_OR my_or_6 (.in_1(my_or_3_out_3), .in_2(my_or_4_out_3), .out_3(my_or_6_out_3));
  My_OR my_or_7 (.in_1(my_or_5_out_3), .in_2(my_or_6_out_3), .out_3(out_2));
endmodule

module My_Mux4Way4 (
  input  [1:0] s0_s1,
  input  [3:0] D0,
  input  [3:0] D1,
  input  [3:0] D2,
  input  [3:0] D3,
  output [3:0] out_6
);

  wire [3:0] my_mux4_1_out_4, my_mux4_2_out_4;

  My_Mux4 my_mux4_1 (.in_1(D0), .in_2(D1), .in_3(s0_s1[1]), .out_4(my_mux4_1_out_4));
  My_Mux4 my_mux4_2 (.in_1(D2), .in_2(D3), .in_3(s0_s1[1]), .out_4(my_mux4_2_out_4));
  My_Mux4 my_mux4_3 (.in_1(my_mux4_1_out_4), .in_2(my_mux4_2_out_4), .in_3(s0_s1[0]), .out_4(out_6));
endmodule

module My_Mux8Way4 (
  input  [2:0] s0_s1_s2,
  input  [3:0] D0,
  input  [3:0] D1,
  input  [3:0] D2,
  input  [3:0] D3,
  input  [3:0] D4,
  input  [3:0] D5,
  input  [3:0] D6,
  input  [3:0] D7,
  output [3:0] out_10
);

  wire [3:0] my_mux4way4_1_out_6, my_mux4way4_2_out_6;

  My_Mux4Way4 my_mux4way4_1 (.D0(D0), .D1(D1), .s0_s1(s0_s1_s2[1:0]), .D2(D2), .D3(D3), .out_6(my_mux4way4_1_out_6));
  My_Mux4Way4 my_mux4way4_2 (.D0(D4), .D1(D5), .s0_s1(s0_s1_s2[1:0]), .D2(D6), .D3(D7), .out_6(my_mux4way4_2_out_6));
  My_Mux4 my_mux4_1 (.in_1(my_mux4way4_1_out_6), .in_2(my_mux4way4_2_out_6), .in_3(s0_s1_s2[2]), .out_4(out_10));
endmodule

module My_DMux4 (
  input  in,
  input  [1:0] in_2,
  output a,
  output b,
  output c,
  output d
);

  wire my_dmux_1_a, my_dmux_1_b;

  My_DMux my_dmux_1 (.in(in), .a(my_dmux_1_a), .b(my_dmux_1_b), .sel(in_2[1]));
  My_DMux my_dmux_2 (.in(my_dmux_1_a), .a(a), .b(b), .sel(in_2[0]));
  My_DMux my_dmux_3 (.in(my_dmux_1_b), .a(c), .b(d), .sel(in_2[0]));
endmodule

module My_DMux8 (
  input  in,
  input  [2:0] in_2,
  output a,
  output b,
  output c,
  output d,
  output e,
  output f,
  output g,
  output h
);

  wire my_dmux4_1_a, my_dmux4_1_b, my_dmux4_1_c, my_dmux4_1_d;

  My_DMux4 my_dmux4_1 (
    .in(in), .a(my_dmux4_1_a), .b(my_dmux4_1_b), .c(my_dmux4_1_c), .d(my_dmux4_1_d), .in_2(in_2[2:1]));
  My_DMux my_dmux_1 (.in(my_dmux4_1_a), .a(a), .b(b), .sel(in_2[0]));
  My_DMux my_dmux_2 (.in(my_dmux4_1_b), .a(c), .b(d), .sel(in_2[0]));
  My_DMux my_dmux_3 (.in(my_dmux4_1_c), .a(e), .b(f), .sel(in_2[0]));
  My_DMux my_dmux_4 (.in(my_dmux4_1_d), .a(g), .b(h), .sel(in_2[0]));
endmodule
