// Logisim project Home Work 2.circ as structural Verilog: 15 circuits, main circuit main
module main (
  input  [3:0] in_1,
  output out_2
);

  BitSelector #(.width(4)) bitselector_1 (.in(in_1), .out(out_2), .sel(2'b11));
endmodule

module HalfAdder (
  input  a,
  input  b,
  output sum,
  output carry
);

  xor xor_1 (sum, a, b);
  and and_1 (carry, a, b);
endmodule

module FullAdder (
  input  a,
  input  b,
  input  c,
  output sum,
  output carry
);

  wire halfadder_1_carry, halfadder_1_sum, halfadder_2_carry;

  HalfAdder halfadder_1 (.a(a), .b(b), .sum(halfadder_1_sum), .carry(halfadder_1_carry));
  HalfAdder halfadder_2 (.a(halfadder_1_sum), .b(c), .sum(sum), .carry(halfadder_2_carry));
  or or_1 (carry, halfadder_1_carry, halfadder_2_carry);
endmodule

module CPA (
  input  [3:0] a,
  input  [3:0] b,
  input  c,
  output [3:0] sum,
  output carry
);

  wire fulladder_1_carry, fulladder_2_carry, fulladder_3_carry;

  FullAdder fulladder_1 (.a(a[0]), .b(b[0]), .c(c), .sum(sum[0]), .carry(fulladder_1_carry));
  FullAdder fulladder_2 (.a(a[1]), .b(b[1]), .c(fulladder_1_carry), .sum(sum[1]), .carry(fulladder_2_carry));
  FullAdder fulladder_3 (.a(a[2]), .b(b[2]), .c(fulladder_2_carry), .sum(sum[2]), .carry(fulladder_3_carry));
  FullAdder fulladder_4 (.a(a[3]), .b(b[3]), .c(fulladder_3_carry), .sum(sum[3]), .carry(carry));
endmodule

module Incrementer (
  input  [3:0] in,
  output [3:0] sum,
  output carry
);

  CPA cpa_1 (.a(in), .b(4'b0001), .c(1'b0), .sum(sum), .carry(carry));
endmodule

module Subtractor (
  input  [3:0] a,
  input  [3:0] b,
  output [3:0] out
);

  wire [3:0] not_1_out;

  assign not_1_out = ~b;  // NOT_Gate not_1, 4 bits wide
  CPA cpa_1 (.a(a), .b(not_1_out), .c(1'b1), .sum(out));  // open: carry
endmodule

module Addition_and_subtraction (
  input  [3:0] a,
  input  [3:0] b,
  input  K,
  output [3:0] out,
  output out_5
);

  wire cpa_1_carry, not_2_out;
  wire [3:0] multiplexer_1_out, not_1_out;

  assign not_1_out = ~b;  // NOT_Gate not_1, 4 bits wide
  Multiplexer #(.width(4), .enable("false")) multiplexer_1 (.in0(b), .in1(not_1_out), .out(multiplexer_1_out), .sel(K));
  CPA cpa_1 (.a(a), .b(multiplexer_1_out), .c(K), .sum(out), .carry(cpa_1_carry));
  not not_2 (not_2_out, K);
  and and_1 (out_5, cpa_1_carry, not_2_out);
endmodule

module Addition_and_subtraction_2 (
  input  [3:0] a,
  input  [3:0] b,
  input  K,
  output [3:0] out
);

  wire [3:0] multiplexer_1_out, not_1_out;

  assign not_1_out = ~b;  // NOT_Gate not_1, 4 bits wide
  Multiplexer #(.width(4), .enable("false")) multiplexer_1 (.in0(b), .in1(not_1_out), .out(multiplexer_1_out), .sel(K));
  CPA cpa_1 (.a(a), .b(multiplexer_1_out), .c(K), .sum(out));  // open: carry
endmodule

module Overflow (
  input  [3:0] a,
  input  [3:0] b,
  input  K,
  output [3:0] out,
  output V
);

  wire and_1_out, and_2_out, not_2_out, not_3_out, not_4_out;
  wire [3:0] multiplexer_1_out, not_1_out;

  Multiplexer #(.width(4), .enable("false")) multiplexer_1 (.in0(b), .in1(not_1_out), .out(multiplexer_1_out), .sel(K));
  assign not_1_out = ~b;  // NOT_Gate not_1, 4 bits wide
  CPA cpa_1 (.a(a), .b(multiplexer_1_out), .c(K), .sum(out));  // open: carry
  not not_2 (not_2_out, a[3]);
  not not_3 (not_3_out, multiplexer_1_out[3]);
  not not_4 (not_4_out, out[3]);
  and and_1 (and_1_out, not_2_out, not_3_out, out[3]);
  and and_2 (and_2_out, a[3], multiplexer_1_out[3], not_4_out);
  or or_1 (V, and_1_out, and_2_out);
endmodule

module equality_comparator (
  input  [3:0] a,
  input  [3:0] b,
  output out
);

  wire [3:0] xnor_1_out;

  assign xnor_1_out = ~(a ^ b);  // XNOR_Gate xnor_1, 4 bits wide
  and and_1 (out, xnor_1_out[0], xnor_1_out[1], xnor_1_out[2], xnor_1_out[3]);
endmodule

module magnitude_comparator (
  input  [3:0] a,
  input  [3:0] b,
  output out
);

  wire [3:0] addition_and_subtraction_1_out;

  Addition_and_subtraction addition_and_subtraction_1 (
    .a(a), .b(b), .K(1'b1), .out(addition_and_subtraction_1_out));  // open: out_5
  BitSelector #(.width(4)) bitselector_1 (.in(addition_and_subtraction_1_out), .out(out), .sel(2'b11));
endmodule

module Synthesized_comparator (
  input  [3:0] a,
  input  [3:0] b,
  output eq,
  output neq,
  output less,
  output more_or_eq,
  output more,
  output less_or_eq
);

  equality_comparator equality_comparator_1 (.a(a), .b(b), .out(eq));
  magnitude_comparator magnitude_comparator_1 (.a(a), .b(b), .out(less));
  magnitude_comparator magnitude_comparator_2 (.a(b), .b(a), .out(more));
  not not_1 (neq, eq);
  not not_2 (more_or_eq, less);
  not not_3 (less_or_eq, more);
endmodule

module ALU_0_0 (
  input  [31:0] A,
  input  [31:0] B,
  input  [2:0] ALU_control,
  output [31:0] Result,
  output Zero,
  output Negative,
  output Overflow
);

  wire comparator_1_lt;
  wire [31:0] adder_1_out, and_1_out, and_2_out, bit_extender_1_out, not_1_out, not_2_out, or_1_out,
       or_2_out, subtractor_1_out;

  assign and_1_out = A & B;  // AND_Gate and_1, 32 bits wide
  assign or_1_out = A | B;  // OR_Gate or_1, 32 bits wide
  Adder #(.width(32)) adder_1 (.a(A), .b(B), .out(adder_1_out));  // open: cin, cout
  assign and_2_out = A & not_1_out;  // AND_Gate and_2, 32 bits wide
  assign not_1_out = ~B;  // NOT_Gate not_1, 32 bits wide
  assign or_2_out = A | not_2_out;  // OR_Gate or_2, 32 bits wide
  assign not_2_out = ~B;  // NOT_Gate not_2, 32 bits wide
  Subtractor_part #(.width(32)) subtractor_1 (.a(A), .b(B), .out(subtractor_1_out));  // open: bin, bout
  Comparator #(.width(32), .mode("unsigned")) comparator_1 (.a(A), .b(B), .lt(comparator_1_lt));  // open: gt, eq
  assign bit_extender_1_out = {{31{1'b0}}, comparator_1_lt};  // Bit_Extender bit_extender_1
  Multiplexer #(.select(3), .width(32), .enable("false")) multiplexer_1 (
    .in0(and_1_out), .in1(or_1_out), .in2(adder_1_out), .in4(and_2_out), .in5(or_2_out),
    .in6(subtractor_1_out), .in7(bit_extender_1_out), .out(Result), .sel(ALU_control));  // open: in3
  Or32 or32_1 (.in_1(Result), .out_2(Zero));
  BitSelector #(.width(32)) bitselector_1 (.in(Result), .out(Negative), .sel({5{1'b1}}));
endmodule

module Or32 (
  input  [31:0] in_1,
  output out_2
);

  or or_1 (out_2, in_1[0], in_1[1], in_1[2], in_1[3], in_1[4], in_1[5], in_1[6], in_1[7], in_1[8], in_1[9], in_1[10], in_1[11], in_1[12], in_1[13], in_1[14], in_1[15], in_1[16], in_1[17], in_1[18], in_1[19], in_1[20], in_1[21], in_1[22], in_1[23], in_1[24], in_1[25], in_1[26], in_1[27], in_1[28], in_1[29], in_1[30], in_1[31]);
endmodule

module ALU (
  input  [31:0] a,
  input  [31:0] b,
  input  [2:0] ALU_controller,
  output [31:0] out_4,
  output out_5
);

  wire [31:0] adder_1_out, and_1_out, bit_extender_1_out, multiplexer_1_out, not_1_out, or_1_out;

  Multiplexer #(.width(32), .enable("false")) multiplexer_1 (
    .in0(b), .in1(not_1_out), .out(multiplexer_1_out), .sel(ALU_controller[2]));
  assign not_1_out = ~b;  // NOT_Gate not_1, 32 bits wide
  assign and_1_out = a & multiplexer_1_out;  // AND_Gate and_1, 32 bits wide
  assign or_1_out = a | multiplexer_1_out;  // OR_Gate or_1, 32 bits wide
  Adder #(.width(32)) adder_1 (.a(a), .b(multiplexer_1_out), .out(adder_1_out), .cin(ALU_controller[2]), .cout(out_5));
  Bit_Extender #(.in_width(32), .out_width(32)) bit_extender_1 (.in(adder_1_out), .out(bit_extender_1_out));
  Multiplexer #(.select(2), .width(32), .enable("false")) multiplexer_2 (
    .in0(and_1_out), .in1(or_1_out), .in2(adder_1_out), .in3(bit_extender_1_out), .out(out_4),
    .sel(ALU_controller[1:0]));
endmodule
