// Logisim project Home Work 5.circ as structural Verilog
module Decode (
  input  [31:0] in_1,
  output [5:0] funct,
  output [4:0] shamt,
  output [4:0] rd,
  output [4:0] rt,
  output [4:0] rs,
  output [15:0] immediate,
  output [25:0] Adress,
  output [5:0] OP
);


  assign Adress = in_1[25:0];
  assign funct = in_1[5:0];
  assign immediate = in_1[15:0];
  assign OP = in_1[31:26];
  assign rd = in_1[15:11];
  assign rs = in_1[25:21];
  assign rt = in_1[20:16];
  assign shamt = in_1[10:6];
endmodule

module addu (
  input  in_1,
  output [31:0] out_2
);

  wire alu_1_p4, ALUSrc, and_1_out, Branch, clock, formadress_1_p2, instructiondecode_1_p2,
       instructiondecode_1_p6, Jump, main_control_block_1_aluop0, main_control_block_1_aluop1, MemRead,
       MemToReg, MemWrite, RegDST, registerfile_1_p6, RegWrite;
  wire [3:0] ALU_Operation;
  wire [4:0] instructiondecode_1_p3, instructiondecode_1_p4, multiplexer_1_out;
  wire [5:0] OP;
  wire [15:0] instructiondecode_1_p5;
  wire [31:0] adder_1_out, adder_2_out, alu_1_p5, bit_extender_1_out, jumpaddr_1_p3, mips_ram_1_p3,
       multiplexer_2_out, multiplexer_3_out, multiplexer_4_out, register_1_q, registerfile_1_p1,
       registerfile_1_p7, shifter_1_out;

  Clock clock_1 (.out(clock));
  Register #(.width(32)) register_1 (.D(multiplexer_4_out), .Q(register_1_q), .clk(clock), .clr(in_1));  // open: en
  Main_Control_Block main_control_block_1 (
    .RegDst(RegDST), .ALUSrc(ALUSrc), .MemtoReg(MemToReg), .RegWrite(RegWrite), .MemRead(MemRead),
    .MemWrite(MemWrite), .Branch(Branch), .ALUOp1(main_control_block_1_aluop1),
    .ALUOp0(main_control_block_1_aluop0), .in_1(OP));
  Adder #(.width(32)) adder_1 (.a(32'h4), .b(register_1_q), .out(adder_1_out));  // open: cin, cout
  // MIPSProgramROM mipsprogramrom_1: pin names not known; wires that end beside it: register_1_q, Jump, out_2, out_2
  // InstructionDecode instructiondecode_1: pin names not known; wires that end beside it: OP, instructiondecode_1_p2, instructiondecode_1_p3, instructiondecode_1_p4, instructiondecode_1_p5, instructiondecode_1_p6, clock
  Multiplexer #(.width(5), .enable("false")) multiplexer_1 (
    .in0(instructiondecode_1_p3), .in1(instructiondecode_1_p4), .out(multiplexer_1_out), .sel(RegDST));
  assign bit_extender_1_out = {{16{1'b0}}, instructiondecode_1_p5};  // Bit_Extender bit_extender_1
  // RegisterFile registerfile_1: pin names not known; wires that end beside it: registerfile_1_p1, RegWrite, instructiondecode_1_p2, multiplexer_1_out, instructiondecode_1_p3, registerfile_1_p6, registerfile_1_p7
  Multiplexer #(.width(32), .enable("false")) multiplexer_2 (
    .in0(registerfile_1_p7), .in1(bit_extender_1_out), .out(multiplexer_2_out), .sel(ALUSrc));
  Shifter #(.width(32)) shifter_1 (.in(bit_extender_1_out), .\dist (5'b00010), .out(shifter_1_out));
  // ALU alu_1: pin names not known; wires that end beside it: registerfile_1_p6, multiplexer_2_out, ALU_Operation, alu_1_p4, alu_1_p5
  Adder #(.width(32)) adder_2 (.a(adder_1_out), .b(shifter_1_out), .out(adder_2_out));  // open: cin, cout
  // JumpAddr jumpaddr_1: pin names not known; wires that end beside it: instructiondecode_1_p6, adder_1_out, jumpaddr_1_p3
  Multiplexer #(.width(32), .enable("false")) multiplexer_3 (
    .in0(adder_1_out), .in1(adder_2_out), .out(multiplexer_3_out), .sel(and_1_out));
  and and_1 (and_1_out, Branch, alu_1_p4);
  // FormAdress formadress_1: pin names not known; wires that end beside it: alu_1_p5, formadress_1_p2, formadress_1_p2, registerfile_1_p7, MemWrite
  Multiplexer #(.width(32), .enable("false")) multiplexer_4 (
    .in0(multiplexer_3_out), .in1(jumpaddr_1_p3), .out(multiplexer_4_out), .sel(Jump));
  // MIPS_RAM mips_ram_1: pin names not known; wires that end beside it: clock, MemRead, mips_ram_1_p3
  Multiplexer #(.width(32), .enable("false")) multiplexer_5 (
    .in0(alu_1_p5), .in1(mips_ram_1_p3), .out(registerfile_1_p1), .sel(MemToReg));

  // Other names for the same wires on the sheet: reset = in_1
endmodule

module Main_Control_Block (
  input  [5:0] in_1,
  output RegDst,
  output ALUSrc,
  output MemtoReg,
  output RegWrite,
  output MemRead,
  output MemWrite,
  output Branch,
  output ALUOp1,
  output ALUOp0
);

  wire not_2_out, not_3_out, not_4_out, not_5_out, not_6_out;

  not not_1 (RegDst, in_1[1]);
  not not_2 (not_2_out, in_1[3]);
  not not_3 (not_3_out, in_1[2]);
  not not_4 (not_4_out, in_1[3]);
  not not_5 (not_5_out, in_1[2]);
  not not_6 (not_6_out, in_1[1]);
  and and_1 (RegWrite, not_2_out, not_3_out);
  and and_2 (MemRead, not_4_out, in_1[1]);
  and and_3 (ALUOp1, not_5_out, not_6_out);

  assign ALUOp0 = in_1[2];
  assign ALUSrc = in_1[1];
  assign Branch = in_1[2];
  assign MemtoReg = in_1[1];
  assign MemWrite = in_1[3];
endmodule

module Control_Panel (
  input  [1:0] in_1,
  input  [5:0] in_2
);
endmodule
